// Logisim project HA.circ as structural Verilog: 2 circuits, main circuit Half Adder
module Half_Adder (
  input  a,
  input  b,
  output S,
  output C
);

  wire and_2_out, and_3_out, not_1_out, not_2_out;

  not not_1 (not_1_out, a);
  not not_2 (not_2_out, b);
  and and_1 (C, a, b);
  and and_2 (and_2_out, not_1_out, b);
  or or_1 (S, and_2_out, and_3_out);
  and and_3 (and_3_out, a, not_2_out);

  // Notes on the sheet:
  //   Half Adder
  //   Tanishq Agarwal 211B326
  //   Januray 3rd, 2024
endmodule

module Full_Adder (
  input  I_P_A,
  input  I_P_B,
  input  I_P_C,
  output SUM,
  output Carry
);

  wire HA_2_c, HA_c, HA_s;

  Half_Adder HA (.a(I_P_B), .b(I_P_C), .S(HA_s), .C(HA_c));
  Half_Adder HA_2 (.a(I_P_A), .b(HA_s), .S(SUM), .C(HA_2_c));
  or or_1 (Carry, HA_2_c, HA_c);

  // Notes on the sheet:
  //   Full Adder using Half Adders
  //   Tanishq Agarwal
  //   January 3rd, 2024
endmodule
