// Logisim project L1.circ as structural Verilog: 4 circuits, main circuit L1EX1
module L1EX1 (
  input  a,
  input  [3:0] a_2,
  input  b,
  input  [3:0] b_2,
  output c,
  output [3:0] c_2,
  output d,
  output [3:0] d_2,
  output e,
  output [3:0] e_2,
  output f,
  output [3:0] f_2,
  output g,
  output [3:0] g_2
);

  wire and_2_out, and_3_out, not_2_out, not_3_out, not_4_out, not_5_out;
  wire [3:0] and_5_out, and_6_out, not_7_out, not_8_out, not_9_out, not_10_out;

  not not_1 (c, a);
  and and_1 (d, a, b);
  or or_1 (e, b, a);
  not not_2 (not_2_out, a);
  not not_3 (not_3_out, b);
  not not_4 (not_4_out, a);
  not not_5 (not_5_out, b);
  or or_2 (f, not_2_out, not_3_out);
  and and_2 (and_2_out, not_4_out, b);
  and and_3 (and_3_out, a, not_5_out);
  or or_3 (g, and_2_out, and_3_out);
  assign c_2 = ~a_2;  // NOT_Gate not_6, 4 bits wide
  assign d_2 = a_2 & b_2;  // AND_Gate and_4, 4 bits wide
  assign e_2 = b_2 | a_2;  // OR_Gate or_4, 4 bits wide
  assign not_7_out = ~a_2;  // NOT_Gate not_7, 4 bits wide
  assign not_8_out = ~b_2;  // NOT_Gate not_8, 4 bits wide
  assign not_9_out = ~a_2;  // NOT_Gate not_9, 4 bits wide
  assign not_10_out = ~b_2;  // NOT_Gate not_10, 4 bits wide
  assign f_2 = not_7_out | not_8_out;  // OR_Gate or_5, 4 bits wide
  assign and_5_out = not_9_out & b_2;  // AND_Gate and_5, 4 bits wide
  assign and_6_out = a_2 & not_10_out;  // AND_Gate and_6, 4 bits wide
  assign g_2 = and_5_out | and_6_out;  // OR_Gate or_6, 4 bits wide

  // Notes on the sheet:
  //   1 BIT ALL IN ONE LOGIC GATE Data Width-1 
  //   1 BIT ALL IN ONE LOGIC GATE 8 DATA WIDTH
endmodule

module L1EX2 (
  input  A,
  input  [7:0] A_2,
  input  B,
  input  [7:0] B_2,
  input  [7:0] X,
  input  X_2,
  input  [7:0] Y,
  input  Y_2,
  output C,
  output [7:0] C_2
);

  wire and_1_out, and_2_out, and_3_out, and_4_out, not_1_out, not_2_out, not_3_out, not_4_out, not_5_out,
       not_6_out;
  wire [7:0] and_5_out, and_6_out, and_7_out, and_8_out, not_7_out, not_8_out, not_9_out, not_10_out,
       not_11_out, not_12_out;

  not not_1 (not_1_out, X_2);
  not not_2 (not_2_out, Y_2);
  not not_3 (not_3_out, X_2);
  not not_4 (not_4_out, Y_2);
  not not_5 (not_5_out, A);
  not not_6 (not_6_out, Y_2);
  and and_1 (and_1_out, A, not_1_out, not_2_out);
  and and_2 (and_2_out, B, not_3_out, not_4_out);
  and and_3 (and_3_out, not_5_out, X_2, Y_2);
  and and_4 (and_4_out, B, X_2, not_6_out);
  or or_1 (C, and_1_out, and_2_out, and_3_out, and_4_out);
  assign not_7_out = ~X;  // NOT_Gate not_7, 8 bits wide
  assign not_8_out = ~Y;  // NOT_Gate not_8, 8 bits wide
  assign not_9_out = ~X;  // NOT_Gate not_9, 8 bits wide
  assign not_10_out = ~Y;  // NOT_Gate not_10, 8 bits wide
  assign not_11_out = ~A_2;  // NOT_Gate not_11, 8 bits wide
  assign not_12_out = ~Y;  // NOT_Gate not_12, 8 bits wide
  assign and_5_out = A_2 & not_7_out & not_8_out;  // AND_Gate and_5, 8 bits wide
  assign and_6_out = B_2 & not_9_out & not_10_out;  // AND_Gate and_6, 8 bits wide
  assign and_7_out = not_11_out & X & Y;  // AND_Gate and_7, 8 bits wide
  assign and_8_out = B_2 & X & not_12_out;  // AND_Gate and_8, 8 bits wide
  assign C_2 = and_5_out | and_6_out | and_7_out | and_8_out;  // OR_Gate or_2, 8 bits wide

  // Notes on the sheet:
  //   1 BIT AIO GATE
  //   Input Lines
  //   Select Lines
  //   Select Lines
  //   8 BIT AIO GATE
  //   Input Lines
endmodule

module L1EX3 (
  input  X,
  input  Y,
  input  Z,
  output F
);

  wire and_1_out, and_2_out, and_3_out;

  and and_1 (and_1_out, X, Y);
  and and_2 (and_2_out, Y, Z);
  or or_1 (F, and_1_out, and_2_out, and_3_out);
  and and_3 (and_3_out, X, Z);

  // Notes on the sheet:
  //   Input Bits
  //   Majority Selector Output Bit
endmodule

module L1EX4 (
  input  X,
  input  Y,
  input  Z,
  output A,
  output B,
  output C
);

  wire and_1_out, and_2_out, and_3_out, and_4_out, and_5_out, and_6_out, and_7_out, not_1_out, not_2_out,
       not_3_out, not_4_out, not_5_out, not_6_out;

  Hex_Digit_Display hex_digit_display_1 (.value({1'b0, X, Y, Z}));  // open: dp
  and and_1 (and_1_out, X, Z);
  and and_2 (and_2_out, X, Y);
  and and_3 (and_3_out, Y, Z);
  not not_1 (not_1_out, X);
  not not_2 (not_2_out, Y);
  not not_3 (not_3_out, X);
  not not_4 (not_4_out, Z);
  not not_5 (not_5_out, Y);
  not not_6 (not_6_out, Z);
  not not_7 (C, Z);
  or or_1 (A, and_1_out, and_2_out, and_3_out);
  and and_4 (and_4_out, not_1_out, not_2_out, Z);
  and and_5 (and_5_out, not_3_out, Y, not_4_out);
  and and_6 (and_6_out, X, not_5_out, not_6_out);
  and and_7 (and_7_out, X, Y, Z);
  or or_2 (B, and_4_out, and_5_out, and_6_out, and_7_out);
  Hex_Digit_Display hex_digit_display_2 (.value({1'b0, A, B, C}));  // open: dp
endmodule
