// Logisim project L2.circ as structural Verilog: 8 circuits, main circuit HA
module HA (
  input  a,
  input  b,
  output S,
  output C
);

  wire and_2_out, and_3_out, not_1_out, not_2_out;

  not not_1 (not_1_out, a);
  not not_2 (not_2_out, b);
  and and_1 (C, a, b);
  and and_2 (and_2_out, not_1_out, b);
  or or_1 (S, and_2_out, and_3_out);
  and and_3 (and_3_out, a, not_2_out);

  // Notes on the sheet:
  //   Half Adder
  //   Tanishq Agarwal 211B326
endmodule

module FA (
  input  I_P_A,
  input  I_P_B,
  input  I_P_C,
  output SUM,
  output Carry
);

  wire ha_1_c, ha_1_s, ha_2_c;

  HA ha_1 (.a(I_P_B), .b(I_P_C), .S(ha_1_s), .C(ha_1_c));
  HA ha_2 (.a(I_P_A), .b(ha_1_s), .S(SUM), .C(ha_2_c));
  or or_1 (Carry, ha_2_c, ha_1_c);

  // Notes on the sheet:
  //   Full Adder using Half Adders
  //   Tanishq Agarwal
endmodule

module HS (
  input  a,
  input  b,
  output Diff,
  output Borrow
);

  wire and_2_out, and_3_out, not_1_out, not_2_out, not_3_out;

  not not_1 (not_1_out, a);
  not not_2 (not_2_out, b);
  and and_1 (Borrow, a, not_3_out);
  not not_3 (not_3_out, b);
  and and_2 (and_2_out, not_1_out, b);
  or or_1 (Diff, and_2_out, and_3_out);
  and and_3 (and_3_out, a, not_2_out);

  // Notes on the sheet:
  //   Half Substractor
  //   Tanishq Agarwal 211B326
endmodule

module FS (
  input  a,
  input  b,
  input  c,
  output Diff,
  output Borrow
);

  wire hs_1_borrow, hs_1_diff, hs_2_borrow;

  HS hs_1 (.a(b), .b(c), .Diff(hs_1_diff), .Borrow(hs_1_borrow));
  HS hs_2 (.a(a), .b(hs_1_diff), .Diff(Diff), .Borrow(hs_2_borrow));
  or or_1 (Borrow, hs_2_borrow, hs_1_borrow);
endmodule

module L2EX1 (
  input  a,
  input  a_2,
  input  b,
  input  b_2,
  output Diff,
  output S,
  output Borrow,
  output C
);

  wire and_2_out, and_3_out, and_5_out, and_6_out, not_1_out, not_2_out, not_3_out, not_4_out, not_5_out;

  not not_1 (not_1_out, a_2);
  not not_2 (not_2_out, b_2);
  and and_1 (C, a_2, b_2);
  and and_2 (and_2_out, not_1_out, b_2);
  or or_1 (S, and_2_out, and_3_out);
  and and_3 (and_3_out, a_2, not_2_out);
  not not_3 (not_3_out, a);
  not not_4 (not_4_out, b);
  and and_4 (Borrow, a, not_5_out);
  not not_5 (not_5_out, b);
  and and_5 (and_5_out, not_3_out, b);
  and and_6 (and_6_out, a, not_4_out);
  or or_2 (Diff, and_5_out, and_6_out);

  // Notes on the sheet:
  //   Half Adder
  //   Tanishq Agarwal 211B326
  //   Half Substractor
endmodule

module L2EX2 (
  input  I_P_A,
  input  I_P_A_2,
  input  I_P_B,
  input  I_P_B_2,
  input  I_P_C,
  input  I_P_C_2,
  output SUM,
  output SUM_2,
  output Carry,
  output Carry_2
);

  wire and_1_out, and_2_out, ha_1_c, ha_1_s, ha_2_c, xor_1_out;

  xor xor_1 (xor_1_out, I_P_A, I_P_B);
  and and_1 (and_1_out, I_P_C, xor_1_out);
  and and_2 (and_2_out, I_P_A, I_P_B);
  xor xor_2 (SUM_2, xor_1_out, I_P_C);
  or or_1 (Carry_2, and_1_out, and_2_out);
  HA ha_1 (.a(I_P_B_2), .b(I_P_C_2), .S(ha_1_s), .C(ha_1_c));
  HA ha_2 (.a(I_P_A_2), .b(ha_1_s), .S(SUM), .C(ha_2_c));
  or or_2 (Carry, ha_2_c, ha_1_c);

  // Notes on the sheet:
  //   Full Adder using Basic Gates
  //   Full Adder using Half Adders
  //   Tanishq Agarwal
endmodule

module L2EX3 (
  input  A0,
  input  A1,
  input  A2,
  input  A3,
  input  B0,
  input  B1,
  input  B2,
  input  B3,
  output CARRY_OUT,
  output S0,
  output S1,
  output S2,
  output S3
);

  wire fa_1_carry, fa_2_carry, ha_1_c;

  Hex_Digit_Display hex_digit_display_1 (.value({A3, A2, A1, A0}));  // open: dp
  Hex_Digit_Display hex_digit_display_2 (.value({B3, B2, B1, B0}));  // open: dp
  HA ha_1 (.a(A0), .b(B0), .S(S0), .C(ha_1_c));
  FA fa_1 (.I_P_A(A1), .I_P_B(B1), .I_P_C(ha_1_c), .SUM(S1), .Carry(fa_1_carry));
  FA fa_2 (.I_P_A(A2), .I_P_B(B2), .I_P_C(fa_1_carry), .SUM(S2), .Carry(fa_2_carry));
  Hex_Digit_Display hex_digit_display_3 (.value({S3, S2, S1, S0}));  // open: dp
  FA fa_3 (.I_P_A(A3), .I_P_B(B3), .I_P_C(fa_2_carry), .SUM(S3), .Carry(CARRY_OUT));
  Hex_Digit_Display hex_digit_display_4 (.value({3'b000, CARRY_OUT}));  // open: dp

  // Notes on the sheet:
  //   4 Bit Binary Adder
endmodule

module L2EX4 (
  input  A0,
  input  A1,
  input  A2,
  input  A3,
  input  in_5,
  input  B0,
  input  B1,
  input  B2,
  input  B3,
  output CARRY_OUT,
  output S0,
  output S1,
  output S2,
  output S3
);

  wire fa_1_carry, fa_2_carry, ha_1_c, xor_1_out, xor_2_out, xor_3_out, xor_4_out;

  Hex_Digit_Display hex_digit_display_1 (.value({A3, A2, A1, A0}));  // open: dp
  Hex_Digit_Display hex_digit_display_2 (.value({B3, B2, B1, B0}));  // open: dp
  xor xor_1 (xor_1_out, in_5, B0);
  xor xor_2 (xor_2_out, in_5, B1);
  xor xor_3 (xor_3_out, in_5, B2);
  xor xor_4 (xor_4_out, in_5, B3);
  HA ha_1 (.a(A0), .b(xor_1_out), .S(S0), .C(ha_1_c));
  FA fa_1 (.I_P_A(A1), .I_P_B(xor_2_out), .I_P_C(ha_1_c), .SUM(S1), .Carry(fa_1_carry));
  FA fa_2 (.I_P_A(A2), .I_P_B(xor_3_out), .I_P_C(fa_1_carry), .SUM(S2), .Carry(fa_2_carry));
  Hex_Digit_Display hex_digit_display_3 (.value({S3, S2, S1, S0}));  // open: dp
  FA fa_3 (.I_P_A(A3), .I_P_B(xor_4_out), .I_P_C(fa_2_carry), .SUM(S3), .Carry(CARRY_OUT));
  Hex_Digit_Display hex_digit_display_4 (.value({3'b000, CARRY_OUT}));  // open: dp

  // Notes on the sheet:
  //   4 Bit Binary Substractor
endmodule
