// Logisim project L3EX1.circ as structural Verilog: 3 circuits, main circuit 2:1 MUX
module _2_1_MUX (
  input  i0,
  input  i1,
  input  s0,
  output out_4
);

  wire and_1_out, and_2_out, not_1_out;

  and and_1 (and_1_out, i0, not_1_out);
  and and_2 (and_2_out, i1, s0);
  not not_1 (not_1_out, s0);
  or or_1 (out_4, and_1_out, and_2_out);

  // Notes on the sheet:
  //   Tanishq Agarwal (211B326)
  //   2:1 MULTIPLEXER
endmodule

module _8_1_MUX (
  input  i0,
  input  i1,
  input  i2,
  input  i3,
  input  i4,
  input  i5,
  input  i6,
  input  i7,
  input  s2,
  input  s1,
  input  s0,
  output out_12
);

  wire n4_1_mux_1_out_7, n4_1_mux_2_out_7;

  _4_1_MUX u_4_1_mux_1 (.i0(i0), .i1(i1), .i2(i2), .i3(i3), .out_7(n4_1_mux_1_out_7), .s0(s0), .s1(s1));
  _4_1_MUX u_4_1_mux_2 (.i0(i4), .i1(i5), .i2(i6), .i3(i7), .out_7(n4_1_mux_2_out_7), .s0(s0), .s1(s1));
  _2_1_MUX u_2_1_mux_1 (.i0(n4_1_mux_1_out_7), .i1(n4_1_mux_2_out_7), .out_4(out_12), .s0(s2));

  // Notes on the sheet:
  //   Tanishq Agarwal (211B326)
  //   8:1 MULTIPLEXER
endmodule

module _4_1_MUX (
  input  i0,
  input  i1,
  input  i2,
  input  i3,
  input  s1,
  input  s0,
  output out_7
);

  wire n2_1_mux_1_out_4, n2_1_mux_2_out_4;

  _2_1_MUX u_2_1_mux_1 (.i0(i0), .i1(i1), .out_4(n2_1_mux_1_out_4), .s0(s0));
  _2_1_MUX u_2_1_mux_2 (.i0(i2), .i1(i3), .out_4(n2_1_mux_2_out_4), .s0(s0));
  _2_1_MUX u_2_1_mux_3 (.i0(n2_1_mux_1_out_4), .i1(n2_1_mux_2_out_4), .out_4(out_7), .s0(s1));

  // Notes on the sheet:
  //   4:1 MULTIPLEXER
  //   Tanishq Agarwal (211B326)
endmodule
