// Logisim project L3EX2.circ as structural Verilog: 3 circuits, main circuit 1:2 DEMUX
// 1:2
module _1_2_DEMUX (
  input  I,
  input  S0,
  output O0,
  output O1
);

  wire not_1_out;

  and and_1 (O0, I, not_1_out);
  not not_1 (not_1_out, S0);
  and and_2 (O1, I, S0);

  // Notes on the sheet:
  //   1:2 DEMULTIPLEXER
  //   Tanishq Agarwal (211B326)
endmodule

// 1:4DMX
module _1_4_DEMUX (
  input  I,
  input  S1,
  input  S0,
  output O0,
  output O1,
  output O2,
  output O3
);

  wire n1_2_demux_1_o0, n1_2_demux_1_o1;

  _1_2_DEMUX u_1_2_demux_1 (.I(I), .S0(S1), .O0(n1_2_demux_1_o0), .O1(n1_2_demux_1_o1));
  _1_2_DEMUX u_1_2_demux_2 (.I(n1_2_demux_1_o0), .S0(S0), .O0(O0), .O1(O1));
  _1_2_DEMUX u_1_2_demux_3 (.I(n1_2_demux_1_o1), .S0(S0), .O0(O2), .O1(O3));

  // Notes on the sheet:
  //   1:4 DEMULTIPLEXER
  //   Tanishq Agarwal (211B326)
endmodule

module _1_8_DEMUX (
  input  I,
  input  S1,
  input  S0,
  output out_4,
  output out_5,
  output out_6,
  output out_7,
  output out_8,
  output out_9,
  output out_10,
  output out_11
);

  wire not_1_out;

  not not_1 (not_1_out, I);
  _1_4_DEMUX u_1_4_demux_1 (.I(not_1_out), .S1(S1), .S0(S0), .O0(out_4), .O1(out_5), .O2(out_6), .O3(out_7));
  _1_4_DEMUX u_1_4_demux_2 (.I(I), .S1(S1), .S0(S0), .O0(out_8), .O1(out_9), .O2(out_10), .O3(out_11));

  // Notes on the sheet:
  //   1:8 DEMULTIPLEXER
  //   Tanishq Agarwal (211B326)
endmodule
