// Logisim project L3EX3.circ as structural Verilog: 1 circuit, main circuit L3EX3
module L3EX3 (
  input  _3,
  input  _2,
  input  _1,
  input  _0,
  output b0,
  output b1
);

  _7_Segment_Display u_7_segment_display_1 (.g(_3), .a(_3), .b(_3), .d(_3), .c(_3));  // open: f, e, dp
  _7_Segment_Display u_7_segment_display_2 (.g(_2), .a(_2), .b(_2), .e(_2), .d(_2));  // open: f, c, dp
  _7_Segment_Display u_7_segment_display_3 (.b(_1), .c(_1));  // open: g, f, a, e, d, dp
  _7_Segment_Display u_7_segment_display_4 (.f(_0), .a(_0), .b(_0), .e(_0), .d(_0), .c(_0));  // open: g, dp
  or or_1 (b0, _1, _3);
  or or_2 (b1, _2, _3);
  Hex_Digit_Display hex_digit_display_1 (.value({3'b000, b1}));  // open: dp
  Hex_Digit_Display hex_digit_display_2 (.value({3'b000, b0}));  // open: dp

  // Notes on the sheet:
  //   Tanishq Agarwal (211B326)
  //   4:2 Encoder
endmodule
