// Logisim project L3EX4.circ as structural Verilog: 2 circuits, main circuit 2:4 DECODER
// 2:4DCDR
module _2_4_DECODER (
  input  en,
  input  I1,
  input  I0,
  output b0,
  output b1,
  output b2,
  output b3
);

  wire not_1_out, not_2_out;

  not not_1 (not_1_out, I1);
  not not_2 (not_2_out, I0);
  and and_1 (b0, not_1_out, en, not_2_out);
  and and_2 (b1, I0, en, not_1_out);
  and and_3 (b2, not_2_out, I1);
  and and_4 (b3, I0, en, I1);
endmodule

module _3_8_DECODER (
  input  i0,
  input  i1,
  input  in_3,
  output b0,
  output b1,
  output b2,
  output b3,
  output b4,
  output b5,
  output b6,
  output b7
);

  wire not_1_out;

  not not_1 (not_1_out, in_3);
  _2_4_DECODER u_2_4_decoder_1 (.en(not_1_out), .I1(i1), .I0(i0), .b0(b0), .b1(b1), .b2(b2), .b3(b3));
  _2_4_DECODER u_2_4_decoder_2 (.en(in_3), .I1(i1), .I0(i0), .b0(b4), .b1(b5), .b2(b6), .b3(b7));

  // Notes on the sheet:
  //   3:8 Decoder
  //   Tanishq Agarwal (211B326)
endmodule
