// Logisim project LE4.circ as structural Verilog: 2 circuits, main circuit EX1
module EX1 (
  input  in_1,
  input  [1:0] in_2,
  input  in_3,
  input  [2:0] in_4,
  input  in_5,
  output out_6,
  output out_7,
  output out_8,
  output out_9
);

  wire not_1_out;

  not not_1 (not_1_out, in_3);
  Multiplexer #(.select(2)) multiplexer_1 (
    .in0(in_3), .in1(not_1_out), .in2(not_1_out), .in3(in_3), .out(out_7), .sel(in_2), .en(in_1));
  Multiplexer #(.select(2)) multiplexer_2 (
    .in0(1'b0), .in1(in_3), .in2(in_3), .in3(1'b1), .out(out_9), .sel(in_2), .en(in_1));
  Multiplexer #(.select(3)) multiplexer_3 (
    .in0(1'b0), .in1(1'b1), .in2(1'b1), .in3(1'b0), .in4(1'b1), .in5(1'b0), .in6(1'b0), .in7(1'b1),
    .out(out_6), .sel(in_4), .en(in_5));
  Multiplexer #(.select(3)) multiplexer_4 (
    .in0(1'b0), .in1(1'b0), .in2(1'b0), .in3(1'b1), .in4(1'b0), .in5(1'b1), .in6(1'b1), .in7(1'b1),
    .out(out_8), .sel(in_4), .en(in_5));

  // Notes on the sheet:
  //   Tanishq Agarwal (211B326)
endmodule

module EX2 (
  input  [7:0] in_1,
  output [2:0] out_2
);

  wire and_1_out, and_2_out, not_1_out, not_2_out, or_1_out;
  wire [3:0] bit_extender_1_out;

  Priority_Encoder priority_encoder_1 (
    .in0(in_1[0]), .in1(in_1[1]), .in2(in_1[2]), .in3(in_1[3]), .in4(in_1[4]), .in5(in_1[5]), .in6(in_1[6]),
    .in7(in_1[7]), .out(out_2));  // open: en_in, gs, en_out
  assign bit_extender_1_out = {{1{1'b0}}, out_2};  // Bit_Extender bit_extender_1
  Hex_Digit_Display hex_digit_display_1 (.value(bit_extender_1_out));  // open: dp
  not not_1 (not_1_out, bit_extender_1_out[0]);
  _7_Segment_Display u_7_segment_display_1 (
    .g(not_1_out), .f(not_1_out), .a(not_1_out), .e(not_1_out), .d(not_1_out));  // open: b, c, dp
  _7_Segment_Display u_7_segment_display_2 (
    .f(bit_extender_1_out[1]), .a(bit_extender_1_out[1]), .b(bit_extender_1_out[1]),
    .e(bit_extender_1_out[1]), .d(bit_extender_1_out[1]), .c(bit_extender_1_out[1]));  // open: g, dp
  and and_1 (and_1_out, bit_extender_1_out[1], bit_extender_1_out[2]);
  not not_2 (not_2_out, bit_extender_1_out[2]);
  and and_2 (and_2_out, not_2_out, bit_extender_1_out[1]);
  _7_Segment_Display u_7_segment_display_3 (
    .g(or_1_out), .f(or_1_out), .a(or_1_out), .b(or_1_out), .e(or_1_out));  // open: d, c, dp
  or or_1 (or_1_out, and_1_out, and_2_out);
  // also tied to GND on the sheet: bit_extender_1_out[3]

  // Notes on the sheet:
  //   Tanishq Agarwal 211B326
endmodule
