// Logisim project LE4EX4.circ as structural Verilog: 1 circuit, main circuit main
module main (
  input  [3:0] in_1,
  input  [3:0] in_2,
  input  [3:0] in_3,
  input  [3:0] in_4
);

  wire and_1_out, and_2_out, nor_1_out, not_1_out, not_2_out, not_3_out, not_4_out, not_5_out, or_1_out,
       or_2_out, or_3_out;
  wire [0:0] and_3_out;

  Hex_Digit_Display hex_digit_display_1 (.value(in_4));  // open: dp
  Hex_Digit_Display hex_digit_display_2 (.value(in_3));  // open: dp
  Hex_Digit_Display hex_digit_display_3 (.value(in_2));  // open: dp
  Hex_Digit_Display hex_digit_display_4 (.value(in_1));  // open: dp
  nor nor_1 (nor_1_out, in_1[0], in_1[1], in_1[2], in_1[3], in_2[0], in_2[1], in_2[2], in_2[3]);
  not not_1 (not_1_out, in_1[0]);
  not not_2 (not_2_out, in_1[1]);
  not not_3 (not_3_out, in_2[0]);
  not not_4 (not_4_out, in_1[0]);
  and and_1 (and_1_out, not_1_out, not_2_out, not_3_out);
  and and_2 (and_2_out, in_2[0], in_1[1], not_4_out);
  or or_1 (or_1_out, or_2_out, nor_1_out);
  not not_5 (not_5_out, nor_1_out);
  or or_2 (or_2_out, and_1_out, and_2_out);
  or or_3 (or_3_out, or_2_out, not_5_out);
  Hex_Digit_Display hex_digit_display_5 (.value({3'b000, and_3_out[0]}));  // open: dp
  and and_3 (and_3_out[0], or_1_out, or_3_out);

  // Notes on the sheet:
  //   Tanishq Agarwal 211B326
endmodule
