// Logisim project LE5.circ as structural Verilog: 4 circuits, main circuit EX1
module EX1 (
  input  [3:0] R1,
  input  [3:0] R2,
  input  [3:0] R3,
  input  [3:0] R4,
  input  in_5,
  input  [1:0] S1_S0,
  output [3:0] out_7
);

  Multiplexer #(.select(2), .width(4)) multiplexer_1 (
    .in0(R1), .in1(R2), .in2(R3), .in3(R4), .out(out_7), .sel(S1_S0), .en(in_5));

  // Notes on the sheet:
  //   Tanishq Agarwal 211B326
endmodule

module EX2 (
  input  [3:0] in_1,
  input  [3:0] in_2,
  input  [3:0] in_3,
  input  [3:0] in_4,
  input  in_5,
  input  [1:0] in_6,
  output [3:0] out_7
);

  wire decoder_1_out0, decoder_1_out1, decoder_1_out2, decoder_1_out3;
  wire [3:0] controlled_buffer_1_out, controlled_buffer_2_out, controlled_buffer_3_out,
       controlled_buffer_4_out;

  Decoder #(.select(2)) decoder_1 (
    .out0(decoder_1_out0), .out1(decoder_1_out1), .out2(decoder_1_out2), .out3(decoder_1_out3), .sel(in_6),
    .en(in_5));
  assign controlled_buffer_1_out = decoder_1_out0 ? in_1 : 4'bz;  // Controlled_Buffer controlled_buffer_1
  assign controlled_buffer_2_out = decoder_1_out1 ? in_2 : 4'bz;  // Controlled_Buffer controlled_buffer_2
  assign controlled_buffer_3_out = decoder_1_out2 ? in_3 : 4'bz;  // Controlled_Buffer controlled_buffer_3
  assign controlled_buffer_4_out = decoder_1_out3 ? in_4 : 4'bz;  // Controlled_Buffer controlled_buffer_4
  assign out_7 = controlled_buffer_1_out | controlled_buffer_2_out | controlled_buffer_3_out | controlled_buffer_4_out;  // OR_Gate or_1, 4 bits wide

  // Notes on the sheet:
  //   Tanishq Agarwal 211B326
endmodule

module EX3 (
  input  in_1,
  input  [3:0] in_2,
  input  [1:0] in_3,
  input  [3:0] in_4,
  output [3:0] out_5
);

  wire [3:0] and_1_out, not_1_out, or_1_out, xor_1_out;

  assign not_1_out = ~in_2;  // NOT_Gate not_1, 4 bits wide
  assign and_1_out = in_2 & in_4;  // AND_Gate and_1, 4 bits wide
  assign or_1_out = in_2 | in_4;  // OR_Gate or_1, 4 bits wide
  assign xor_1_out = in_2 ^ in_4;  // XOR_Gate xor_1, 4 bits wide
  Multiplexer #(.select(2), .width(4)) multiplexer_1 (
    .in0(not_1_out), .in1(and_1_out), .in2(or_1_out), .in3(xor_1_out), .out(out_5), .sel(in_3), .en(in_1));

  // Notes on the sheet:
  //   Tanishq Agarwal 211B326
endmodule

module EX4 (
  input  [3:0] I_P_A,
  input  [3:0] I_P_B,
  input  [3:0] in_3,
  input  [1:0] Select
);

  wire [1:0] undriven;
  wire [3:0] multiplexer_1_out;

  Multiplexer #(.select(2), .width(4), .enable("false")) multiplexer_1 (
    .in0({I_P_A[2:0], 1'b0}), .in1({I_P_B[0], I_P_B[3:1]}), .in2({{2{I_P_A[3]}}, I_P_A[2:1]}),
    .in3({I_P_B[2:0], I_P_B[3]}), .out(multiplexer_1_out), .sel(undriven));

  // Notes on the sheet:
  //   Tanishq Agarwal 211B326
endmodule
