// Logisim project LE6EX2.circ as structural Verilog: 1 circuit, main circuit EX2
module EX2 (
  input  a0,
  input  bo,
  input  a1,
  input  b1,
  output out_5,
  output out_6,
  output out_7,
  output out_8
);

  wire adder_1_cout, and_2_out, and_3_out, and_4_out;

  and and_1 (out_5, a0, bo);
  and and_2 (and_2_out, a0, b1);
  and and_3 (and_3_out, a1, b1);
  and and_4 (and_4_out, a1, b1);
  Adder #(.width(1)) adder_1 (.a(and_3_out), .b(and_2_out), .out(out_6), .cout(adder_1_cout));  // open: cin
  Adder #(.width(1)) adder_2 (.a(and_4_out), .b(adder_1_cout), .out(out_7), .cout(out_8));  // open: cin

  // Notes on the sheet:
  //   Tanishq Agarwal 211B326
  //   LAB 6- Q2
endmodule
