// Logisim project LE7.circ as structural Verilog: 3 circuits, main circuit EX1
module EX1 (
  input  Preset,
  input  D,
  input  CLK,
  input  Enable,
  input  Clear,
  output out_6,
  output out_7
);

  wire nand_1_out, nand_2_out, nand_3_out, nand_4_out, nand_5_out, nand_6_out, not_1_out, not_2_out,
       not_3_out;

  not not_1 (not_1_out, Preset);
  nand nand_1 (nand_1_out, D, Enable, CLK);
  nand nand_2 (nand_2_out, CLK, Enable, D);
  not not_2 (not_2_out, Clear);
  not not_3 (not_3_out, CLK);
  nand nand_3 (nand_3_out, nand_1_out, not_1_out, nand_4_out);
  nand nand_4 (nand_4_out, nand_3_out, not_2_out, nand_2_out);
  nand nand_5 (nand_5_out, nand_3_out, not_3_out);
  nand nand_6 (nand_6_out, nand_4_out, not_3_out);
  nand nand_7 (out_6, nand_5_out, not_1_out, out_7);
  nand nand_8 (out_7, out_6, not_2_out, nand_6_out);

  // Notes on the sheet:
  //   D Flip Flop Tanishq Agarwal 211B326
endmodule

module EX2 (
  input  Preset,
  input  Clear,
  input  Right___NOT_Left,
  input  Serial_Input,
  input  Enable,
  output Q0,
  output Q1,
  output Q2,
  output Q3
);

  wire and_1_out, and_2_out, and_3_out, and_4_out, and_5_out, and_6_out, and_7_out, and_8_out, clock_1_out,
       not_1_out, or_1_out, or_2_out, or_3_out, or_4_out;

  not not_1 (not_1_out, Right___NOT_Left);
  Clock clock_1 (.out(clock_1_out));
  and and_1 (and_1_out, Serial_Input, Right___NOT_Left);
  and and_2 (and_2_out, not_1_out, Q1);
  or or_1 (or_1_out, and_1_out, and_2_out);
  and and_3 (and_3_out, Q0, Right___NOT_Left);
  buf and_4 (and_4_out, not_1_out);  // AND_Gate
  or or_2 (or_2_out, and_3_out, and_4_out);
  EX1 ex1_1 (
    .Preset(Preset), .D(or_1_out), .CLK(clock_1_out), .Enable(Enable), .Clear(Clear), .out_6(Q0));  // open: out_7
  and and_5 (and_5_out, Q1, Right___NOT_Left);
  and and_6 (and_6_out, not_1_out, Q3);
  or or_3 (or_3_out, and_5_out, and_6_out);
  EX1 ex1_2 (
    .Preset(Preset), .D(or_2_out), .CLK(clock_1_out), .Enable(Enable), .Clear(Clear), .out_6(Q1));  // open: out_7
  and and_7 (and_7_out, Q2, Right___NOT_Left);
  or or_4 (or_4_out, and_7_out, and_8_out);
  EX1 ex1_3 (
    .Preset(Preset), .D(or_3_out), .CLK(clock_1_out), .Enable(Enable), .Clear(Clear), .out_6(Q2));  // open: out_7
  and and_8 (and_8_out, not_1_out, Serial_Input);
  EX1 ex1_4 (
    .Preset(Preset), .D(or_4_out), .CLK(clock_1_out), .Enable(Enable), .Clear(Clear), .out_6(Q3));  // open: out_7

  // Notes on the sheet:
  //   CLK
endmodule

module EX3 (
  input  CLEAR,
  input  [1:0] S0_S1,
  input  MUX_Enable,
  input  Serial_I_P,
  input  M4,
  input  M3,
  input  M2,
  input  M1,
  output F4,
  output F3,
  output F2,
  output F1
);

  wire clock_1_out, multiplexer_1_out, multiplexer_2_out, multiplexer_3_out, multiplexer_4_out, not_1_out,
       not_2_out;

  Clock clock_1 (.out(clock_1_out));
  not not_1 (not_1_out, CLEAR);
  not not_2 (not_2_out, clock_1_out);
  D_Flip_Flop d_ff_1 (.clk(not_2_out), .D(multiplexer_1_out), .Q(F4), .reset(not_1_out));  // open: Qn, preset, en
  Multiplexer #(.select(2)) multiplexer_1 (
    .in0(M4), .out(multiplexer_1_out), .sel(S0_S1), .en(MUX_Enable));  // open: in1, in2, in3
  D_Flip_Flop d_ff_2 (.clk(not_2_out), .D(multiplexer_2_out), .Q(F3), .reset(not_1_out));  // open: Qn, preset, en
  Multiplexer #(.select(2)) multiplexer_2 (
    .in0(M3), .out(multiplexer_2_out), .sel(S0_S1), .en(MUX_Enable));  // open: in1, in2, in3
  D_Flip_Flop d_ff_3 (.clk(not_2_out), .D(multiplexer_3_out), .Q(F2), .reset(not_1_out));  // open: Qn, preset, en
  Multiplexer #(.select(2)) multiplexer_3 (
    .in0(M2), .out(multiplexer_3_out), .sel(S0_S1), .en(MUX_Enable));  // open: in1, in2, in3
  Multiplexer #(.select(2)) multiplexer_4 (
    .in0(M1), .out(multiplexer_4_out), .sel(S0_S1), .en(MUX_Enable));  // open: in1, in2, in3
  D_Flip_Flop d_ff_4 (.clk(not_2_out), .D(multiplexer_4_out), .Q(F1), .reset(not_1_out));  // open: Qn, preset, en

  // Notes on the sheet:
  //   CLK
endmodule
