// Logisim project LE8.circ as structural Verilog: 5 circuits, main circuit EX1
module EX1 (
  input  EN,
  input  Reset,
  output QA,
  output QB,
  output QC,
  output clock_out
);

  wire and_1_out, clock_in_out, d_ff_1_qn, d_ff_2_qn, d_ff_3_qn;

  Clock clock_in (.out(clock_in_out));
  D_Flip_Flop d_ff_1 (
    .clk(clock_in_out), .D(d_ff_1_qn), .Q(QA), .Qn(d_ff_1_qn), .en(EN), .reset(clock_out));  // open: preset
  or or_1 (clock_out, and_1_out, Reset);
  Hex_Digit_Display hex_digit_display_1 (.value({1'b0, QC, QB, QA}));  // open: dp
  and and_1 (and_1_out, QB, QC);
  D_Flip_Flop d_ff_2 (
    .clk(d_ff_1_qn), .D(d_ff_2_qn), .Q(QB), .Qn(d_ff_2_qn), .en(EN), .reset(clock_out));  // open: preset
  D_Flip_Flop d_ff_3 (
    .clk(d_ff_2_qn), .D(d_ff_3_qn), .Q(QC), .Qn(d_ff_3_qn), .en(EN), .reset(clock_out));  // open: preset

  // Notes on the sheet:
  //   Tanishq Agarwal 211B326
  //   LE8EX1
endmodule

module MOD6 (
  input  clock_in,
  input  EN,
  input  Reset,
  output QA,
  output QB,
  output QC,
  output clock_out
);

  wire and_1_out, d_ff_1_qn, d_ff_2_qn, d_ff_3_qn;

  D_Flip_Flop d_ff_1 (
    .clk(clock_in), .D(d_ff_1_qn), .Q(QA), .Qn(d_ff_1_qn), .en(EN), .reset(clock_out));  // open: preset
  or or_1 (clock_out, and_1_out, Reset);
  and and_1 (and_1_out, QB, QC);
  D_Flip_Flop d_ff_2 (
    .clk(d_ff_1_qn), .D(d_ff_2_qn), .Q(QB), .Qn(d_ff_2_qn), .en(EN), .reset(clock_out));  // open: preset
  D_Flip_Flop d_ff_3 (
    .clk(d_ff_2_qn), .D(d_ff_3_qn), .Q(QC), .Qn(d_ff_3_qn), .en(EN), .reset(clock_out));  // open: preset

  // Notes on the sheet:
  //   Tanishq Agarwal 211B326
  //   LE8MOD6
endmodule

module MOD3 (
  input  clock_in,
  input  EN,
  input  Reset,
  output QA,
  output QB,
  output clock_out
);

  wire and_1_out, d_ff_1_qn, d_ff_2_qn;

  D_Flip_Flop d_ff_1 (
    .clk(clock_in), .D(d_ff_1_qn), .Q(QA), .Qn(d_ff_1_qn), .en(EN), .reset(clock_out));  // open: preset
  or or_1 (clock_out, and_1_out, Reset);
  and and_1 (and_1_out, QB, QA);
  D_Flip_Flop d_ff_2 (
    .clk(d_ff_1_qn), .D(d_ff_2_qn), .Q(QB), .Qn(d_ff_2_qn), .en(EN), .reset(clock_out));  // open: preset

  // Notes on the sheet:
  //   Tanishq Agarwal 211B326
  //   LE8MOD3
endmodule

module MOD10 (
  input  clock_in,
  input  EN,
  input  Reset,
  output QA,
  output QB,
  output QC,
  output QD,
  output clock_out
);

  wire and_1_out, d_ff_1_qn, d_ff_2_qn, d_ff_3_qn, d_ff_4_qn;

  D_Flip_Flop d_ff_1 (
    .clk(clock_in), .D(d_ff_1_qn), .Q(QA), .Qn(d_ff_1_qn), .en(EN), .reset(clock_out));  // open: preset
  or or_1 (clock_out, and_1_out, Reset);
  D_Flip_Flop d_ff_2 (
    .clk(d_ff_1_qn), .D(d_ff_2_qn), .Q(QB), .Qn(d_ff_2_qn), .en(EN), .reset(clock_out));  // open: preset
  and and_1 (and_1_out, QB, QD);
  D_Flip_Flop d_ff_3 (
    .clk(d_ff_2_qn), .D(d_ff_3_qn), .Q(QC), .Qn(d_ff_3_qn), .en(EN), .reset(clock_out));  // open: preset
  D_Flip_Flop d_ff_4 (
    .clk(d_ff_3_qn), .D(d_ff_4_qn), .Q(QD), .Qn(d_ff_4_qn), .en(EN), .reset(clock_out));  // open: preset

  // Notes on the sheet:
  //   Tanishq Agarwal 211B326
  //   LE8MOD10
endmodule

module EX2 (
  input  zero,
  input  EN,
  input  Reset
);

  wire and_1_out, clock_out, mod6_1_clock_out, mod6_2_clock_out, mod10_1_clock_out, mod10_2_clock_out,
       mod10_3_clock_out, or_1_out;
  wire [1:1] mod3_1_qa;
  wire [2:0] mod6_1_qa, mod6_2_qa;
  wire [3:0] mod10_1_qa, mod10_2_qa, mod10_3_qa;

  MOD3 mod3_1 (
    .clock_in(mod10_1_clock_out), .EN(EN), .Reset(or_1_out), .QA(mod3_1_qa[1]), .QB(mod3_1_qa[1]));  // open: clock_out
  Hex_Digit_Display hex_digit_display_1 (.value(mod10_1_qa));  // open: dp
  Hex_Digit_Display hex_digit_display_2 (.value({{2{zero}}, {2{mod3_1_qa[1]}}}));  // open: dp
  MOD10 mod10_1 (
    .clock_in(mod6_1_clock_out), .EN(EN), .clock_out(mod10_1_clock_out), .Reset(or_1_out),
    .QA(mod10_1_qa[0]), .QB(mod10_1_qa[1]), .QC(mod10_1_qa[2]), .QD(mod10_1_qa[3]));
  and and_1 (and_1_out, mod10_1_qa[1], mod3_1_qa[1]);
  Hex_Digit_Display hex_digit_display_3 (.value({zero, mod6_1_qa}));  // open: dp
  MOD6 mod6_1 (
    .clock_in(mod10_2_clock_out), .EN(EN), .clock_out(mod6_1_clock_out), .Reset(or_1_out), .QA(mod6_1_qa[0]),
    .QB(mod6_1_qa[1]), .QC(mod6_1_qa[2]));
  or or_1 (or_1_out, and_1_out, Reset);
  Hex_Digit_Display hex_digit_display_4 (.value(mod10_2_qa));  // open: dp
  MOD10 mod10_2 (
    .clock_in(mod6_2_clock_out), .EN(EN), .clock_out(mod10_2_clock_out), .Reset(or_1_out),
    .QA(mod10_2_qa[0]), .QB(mod10_2_qa[1]), .QC(mod10_2_qa[2]), .QD(mod10_2_qa[3]));
  Hex_Digit_Display hex_digit_display_5 (.value({zero, mod6_2_qa}));  // open: dp
  Hex_Digit_Display hex_digit_display_6 (.value(mod10_3_qa));  // open: dp
  MOD6 mod6_2 (
    .clock_in(mod10_3_clock_out), .EN(EN), .clock_out(mod6_2_clock_out), .Reset(or_1_out), .QA(mod6_2_qa[0]),
    .QB(mod6_2_qa[1]), .QC(mod6_2_qa[2]));
  Clock clock (.out(clock_out));
  MOD10 mod10_3 (
    .clock_in(clock_out), .EN(EN), .clock_out(mod10_3_clock_out), .Reset(or_1_out), .QA(mod10_3_qa[0]),
    .QB(mod10_3_qa[1]), .QC(mod10_3_qa[2]), .QD(mod10_3_qa[3]));

  // Notes on the sheet:
  //   LE8EX2
  //   Tanishq Agarwal 211B326
endmodule
